// Logisim project samuelmacaquinho.circ as structural Verilog: 2 circuits, main circuit main
module main (
  input  A,
  input  B,
  input  C,
  output a_2,
  output b_2,
  output c_2,
  output d,
  output e,
  output f,
  output g
);

  and and_1 (g, ~A, ~B);  // AND_Gate
  or or_1 (b_2, B, ~C);  // OR_Gate
  or or_2 (d, A, C);
  or or_3 (e, C, ~B);  // OR_Gate
  or or_4 (a_2, g, C);

  assign c_2 = b_2;
  assign f = e;
endmodule

module Decodificador_BCD (
  input  A,
  input  B,
  input  C
);

  wire clock_1_out, main_1_a_2, main_1_b_2, main_1_c_2, main_1_d, main_1_e, main_1_f, main_1_g, main_2_a_2,
       main_2_b_2, main_2_c_2, main_2_d, main_2_e, main_2_f, main_2_g;
  wire [2:0] counter_1_q;

  main main_1 (
    .a_2(main_1_a_2), .b_2(main_1_b_2), .c_2(main_1_c_2), .d(main_1_d), .e(main_1_e), .f(main_1_f),
    .g(main_1_g), .A(A), .B(B), .C(C));
  _7_Segment_Display u_7_segment_display_1 (
    .g(main_1_g), .f(main_1_f), .a(main_1_a_2), .b(main_1_b_2), .e(main_1_e), .d(main_1_d), .c(main_1_c_2));  // open: dp
  Clock clock_1 (.out(clock_1_out));
  Counter #(.width(3), .max('h4)) counter_1 (.Q(counter_1_q), .clk(clock_1_out));  // open: load, D, count, carry, clr
  main main_2 (
    .a_2(main_2_a_2), .b_2(main_2_b_2), .c_2(main_2_c_2), .d(main_2_d), .e(main_2_e), .f(main_2_f),
    .g(main_2_g), .A(counter_1_q[2]), .B(counter_1_q[1]), .C(counter_1_q[0]));
  _7_Segment_Display u_7_segment_display_2 (
    .g(main_2_g), .f(main_2_f), .a(main_2_a_2), .b(main_2_b_2), .e(main_2_e), .d(main_2_d), .c(main_2_c_2));  // open: dp
endmodule
